# Fritzing sketch brainz (saved by Fritzing 0.9.3b)
circuit board: 12cm x 7.5cm
breadboards: 1

parts:
  5V = 3.5mm Audio Jack [package=audio-jack]
  GND = 3.5mm Audio Jack [package=audio-jack]
  SHAPE_1 = Rotary Potentiometer (Large) [maximum_resistance=100kΩ package=THT]
  WAVEFORM_1 = Rotary Potentiometer (Large) [maximum_resistance=100kΩ package=THT]
  SHAPE_2 = Rotary Potentiometer (Large) [maximum_resistance=100kΩ package=THT]
  WAVEFORM_2 = Rotary Potentiometer (Large) [maximum_resistance=100kΩ package=THT]
  SHAPE_3 = Rotary Potentiometer (Large) [maximum_resistance=100kΩ package=THT]
  WAVEFORM_3 = Rotary Potentiometer (Large) [maximum_resistance=100kΩ package=THT]
  FREQ_1 = Resistor [tolerance=±5% resistance=220 package=THT]
  FM_1 = Resistor [tolerance=±5% resistance=220 package=THT]
  FREQ_2 = Resistor [tolerance=±5% resistance=220 package=THT]
  FM_2 = Resistor [tolerance=±5% resistance=220 package=THT]
  FREQ_3 = Resistor [tolerance=±5% resistance=220 package=THT]
  FM_3 = Resistor [tolerance=±5% resistance=220 package=THT]
  FREQ_1_2 = Resistor [tolerance=±5% resistance=220 package=THT]
  FM_1_2 = Resistor [tolerance=±5% resistance=220 package=THT]
  FREQ_2_2 = Resistor [tolerance=±5% resistance=220 package=THT]
  FM_2_2 = Resistor [tolerance=±5% resistance=220 package=THT]
  FREQ_3_2 = Resistor [tolerance=±5% resistance=220 package=THT]
  FM_3_2 = Resistor [tolerance=±5% resistance=220 package=THT]

nets:
  N1: 5V.LEFT, SHAPE_1.leg1, WAVEFORM_1.leg1, SHAPE_2.leg1, WAVEFORM_2.leg1, SHAPE_3.leg1, WAVEFORM_3.leg1, FREQ_1.Pin_1, FM_1.Pin_1, FREQ_2.Pin_1, FM_2.Pin_1, FREQ_3.Pin_1, FM_3.Pin_1
  N2: GND.LEFT, SHAPE_1.leg2, WAVEFORM_1.leg2, SHAPE_2.leg2, WAVEFORM_2.leg2, SHAPE_3.leg2, WAVEFORM_3.leg2, FREQ_1_2.Pin_0, FM_1_2.Pin_0, FREQ_2_2.Pin_0, FM_2_2.Pin_0, FREQ_3_2.Pin_0, FM_3_2.Pin_0
  N3: FREQ_1.Pin_0, FREQ_1_2.Pin_1
  N4: FM_1.Pin_0, FM_1_2.Pin_1
  N5: FREQ_2.Pin_0, FREQ_2_2.Pin_1
  N6: FM_2.Pin_0, FM_2_2.Pin_1
  N7: FREQ_3.Pin_0, FREQ_3_2.Pin_1
  N8: FM_3.Pin_0, FM_3_2.Pin_1

notes:
  BRAINZ
