# Fritzing sketch eyez (saved by Fritzing 0.9.3b)
circuit board: 14.3cm x 3.6cm
breadboards: 1

parts:
  F-E1 = PHOTOCELL [package=photocell]
  F-E2 = PHOTOCELL [package=photocell-kit]
  F-E3 = PHOTOCELL [package=photocell-kit]
  F-E4 = PHOTOCELL [package=photocell-kit]
  F-E5 = PHOTOCELL [package=photocell-kit]
  F-E6 = PHOTOCELL [package=photocell-kit]
  R-E1 = Resistor [tolerance=±5% resistance=220 package=THT]
  R-E2 = Resistor [tolerance=±5% resistance=220 package=THT]
  R-E3 = Resistor [tolerance=±5% resistance=220 package=THT]
  R-E4 = Resistor [tolerance=±5% resistance=220 package=THT]
  R-E5 = Resistor [tolerance=±5% resistance=220 package=THT]
  R-E6 = Resistor [tolerance=±5% resistance=220 package=THT]
  5V = Audio Jack (TRS) 3.5mm [package="4Ucon 08780 [THT]"]
  E1 = Audio Jack (TRS) 3.5mm [package="4Ucon 08780 [THT]"]
  E2 = Audio Jack (TRS) 3.5mm [package="4Ucon 08780 [THT]"]
  E3 = Audio Jack (TRS) 3.5mm [package="4Ucon 08780 [THT]"]
  E4 = Audio Jack (TRS) 3.5mm [package="4Ucon 08780 [THT]"]
  E5 = Audio Jack (TRS) 3.5mm [package="4Ucon 08780 [THT]"]
  E6 = Audio Jack (TRS) 3.5mm [package="4Ucon 08780 [THT]"]
  GND = Audio Jack (TRS) 3.5mm [package="4Ucon 08780 [THT]"]

nets:
  N1: F-E1.P$1, F-E2.P$1, F-E3.P$1, F-E4.P$1, F-E5.P$1, F-E6.P$1, 5V.Tip
  N2: F-E1.P$2, R-E1.Pin_0, E1.Tip
  N3: F-E2.P$2, R-E2.Pin_0, E2.Tip
  N4: F-E3.P$2, R-E3.Pin_0, E3.Tip
  N5: F-E4.P$2, R-E4.Pin_0, E4.Tip
  N6: F-E5.P$2, R-E5.Pin_0, E5.Tip
  N7: F-E6.P$2, R-E6.Pin_0, E6.Tip
  N8: R-E1.Pin_1, R-E2.Pin_1, R-E3.Pin_1, R-E4.Pin_1, R-E5.Pin_1, R-E6.Pin_1, GND.Tip

notes:
  EYEZ 1.0
