# Fritzing sketch zpine (saved by Fritzing 0.9.3b)
circuit board: 20cm x 8cm
breadboards: 1

parts:
  Multiplexor_4 = Analog Digital MUX Breakout
  Multiplexor_1 = Analog Digital MUX Breakout
  Multiplexor_2 = Analog Digital MUX Breakout
  Multiplexor_3 = Analog Digital MUX Breakout

nets:
  GND: Multiplexor_4.GND, Multiplexor_4.EN, Multiplexor_1.GND, Multiplexor_1.EN, Multiplexor_2.GND, Multiplexor_2.EN, Multiplexor_3.GND, Multiplexor_3.EN
  VCC: Multiplexor_4.VCC, Multiplexor_1.VCC, Multiplexor_2.VCC, Multiplexor_3.VCC

notes:
  5+
  GND
  A0
  A1
  A2
  A3
  ZPINE 1.0
